# Fritzing sketch Shield (saved by Fritzing 0.9.1b)
circuit board: 9cm x 9cm

parts:
  JOY0 = male pin header, 6 pins [form="♂ (male)"]
  JOY1 = male pin header, 6 pins [form="♂ (male)"]
  A8_A9_A10_A11_A12_A13_A14_A15 = male pin header, 8 pins [form="♂ (male)"]
  7seg = male pin header, 5 pins [form="♂ (male)"]
  13_12_11_10_09_08 = male pin header, 6 pins [form="♂ (male)"]
  14_15_16_17_18_19 = male pin header, 6 pins [form="♂ (male)"]
  I2C = male pin header, 4 pins [form="♂ (male)"]
  53_51_49_47_45_43_41_39_37_35_33_31_29_27_25_23 = male pin header, 16 pins [form="♂ (male)"]
  G3 = male pin header, 8 pins [form="♂ (male)"]
  V3 = male pin header, 8 pins [form="♂ (male)"]
  G4 = male pin header, 5 pins [form="♂ (male)"]
  V4 = male pin header, 5 pins [form="♂ (male)"]
  G6 = male pin header, 6 pins [form="♂ (male)"]
  G7 = male pin header, 6 pins [form="♂ (male)"]
  V7 = male pin header, 6 pins [form="♂ (male)"]
  G9 = male pin header, 16 pins [form="♂ (male)"]
  V9 = male pin header, 16 pins [form="♂ (male)"]
  G10 = male pin header, 16 pins [form="♂ (male)"]
  V10 = male pin header, 16 pins [form="♂ (male)"]
  J8' = male pin header, 4 pins [form="♂ (male)"]
  J8'' = male pin header, 4 pins [form="♂ (male)"]
  J8''' = male pin header, 4 pins [form="♂ (male)"]
  J8'''' = male pin header, 4 pins [form="♂ (male)"]
  J8''''' = male pin header, 4 pins [form="♂ (male)"]
  J8'''''' = male pin header, 4 pins [form="♂ (male)"]
  GND0 = male pin header, 1 pin [form="♂ (male)"]
  GND1 = male pin header, 2 pins [form="♂ (male)"]
  H1 = male pin header, 3 pins [form="♂ (male)"]
  H2 = male pin header, 2 pins [form="♂ (male)"]
  H0 = male pin header, 8 pins [form="♂ (male)"]
  04_03_02_01_00 = male pin header, 5 pins [form="♂ (male)"]
  GND = male pin header, 15 pins [form="♂ (male)"]
  5V = male pin header, 15 pins [form="♂ (male)"]
  3_3V = male pin header, 15 pins [form="♂ (male)"]
  VCC0 = male pin header, 3 pins [form="♂ (male)"]
  GND2 = male pin header, 1 pin [form="♂ (male)"]
  RST = male pin header, 1 pin [form="♂ (male)"]
  VCC1 = male pin header, 2 pins [form="♂ (male)"]
  52_50_48_46_44_42_40_38_36_34_32_30_28_26_24_22 = male pin header, 16 pins [form="♂ (male)"]
  Mega = Arduino Mega 2560 (Rev3)
  V6 = male pin header, 6 pins [form="♂ (male)"]

nets:
  N1: JOY0.pin1, H0.pin1, Mega.A0
  N2: JOY0.pin2, H0.pin2, Mega.A1
  N3: JOY0.pin3, H0.pin3, Mega.A2
  N4: JOY0.pin4, H0.pin4, Mega.A3
  N5: JOY0.pin5, JOY1.pin5, 7seg.pin5, I2C.pin3, G3.pin1, G3.pin2, G3.pin3, G3.pin4, G3.pin5, G3.pin6, G3.pin7, G3.pin8, G4.pin1, G4.pin2, G4.pin3, G4.pin4, G4.pin5, G6.pin1, G6.pin2, G6.pin3, G6.pin4, G6.pin5, G6.pin6, G7.pin1, G7.pin2, G7.pin3, G7.pin4, G7.pin5, G7.pin6, G9.pin1, G9.pin2, G9.pin3, G9.pin4, G9.pin5, G9.pin6, G9.pin7, G9.pin8, G9.pin9, G9.pin10, G9.pin11, G9.pin12, G9.pin13, G9.pin14, G9.pin15, G9.pin16, G10.pin1, G10.pin2, G10.pin3, G10.pin4, G10.pin5, G10.pin6, G10.pin7, G10.pin8, G10.pin9, G10.pin10, G10.pin11, G10.pin12, G10.pin13, G10.pin14, G10.pin15, G10.pin16, J8'.pin3, J8''.pin3, J8'''.pin3, J8''''.pin3, J8'''''.pin3, J8''''''.pin3, GND0.pin1, GND1.pin1, GND1.pin2, GND.pin1, GND.pin2, GND.pin3, GND.pin4, GND.pin5, GND.pin6, GND.pin7, GND.pin8, GND.pin9, GND.pin10, GND.pin11, GND.pin12, GND.pin13, GND.pin14, GND.pin15, VCC0.pin1, GND2.pin1, Mega.GND
  N6: JOY0.pin6, JOY1.pin6, 7seg.pin1, I2C.pin4, V3.pin1, V3.pin2, V3.pin3, V3.pin4, V3.pin5, V3.pin6, V3.pin7, V3.pin8, V4.pin1, V4.pin2, V4.pin3, V4.pin4, V4.pin5, V7.pin1, V7.pin2, V7.pin3, V7.pin4, V7.pin5, V7.pin6, V9.pin1, V9.pin2, V9.pin3, V9.pin4, V9.pin5, V9.pin6, V9.pin7, V9.pin8, V9.pin9, V9.pin10, V9.pin11, V9.pin12, V9.pin13, V9.pin14, V9.pin15, V9.pin16, V10.pin1, V10.pin2, V10.pin3, V10.pin4, V10.pin5, V10.pin6, V10.pin7, V10.pin8, V10.pin9, V10.pin10, V10.pin11, V10.pin12, V10.pin13, V10.pin14, V10.pin15, V10.pin16, J8'.pin4, J8''.pin4, J8'''.pin4, J8''''.pin4, J8'''''.pin4, J8''''''.pin4, 5V.pin1, 5V.pin2, 5V.pin3, 5V.pin4, 5V.pin5, 5V.pin6, 5V.pin7, 5V.pin8, 5V.pin9, 5V.pin10, 5V.pin11, 5V.pin12, 5V.pin13, 5V.pin14, 5V.pin15, VCC0.pin2, VCC1.pin1, VCC1.pin2, Mega.5V, V6.pin1, V6.pin2, V6.pin3, V6.pin4, V6.pin5, V6.pin6
  N7: JOY1.pin1, H0.pin5, Mega.A4
  N8: JOY1.pin2, H0.pin6, Mega.A5
  N9: JOY1.pin3, H0.pin7, Mega.A6
  N10: JOY1.pin4, H0.pin8, Mega.A7
  N11: A8_A9_A10_A11_A12_A13_A14_A15.pin1, Mega.A8
  N12: A8_A9_A10_A11_A12_A13_A14_A15.pin2, Mega.A9
  N13: A8_A9_A10_A11_A12_A13_A14_A15.pin3, Mega.A10
  N14: A8_A9_A10_A11_A12_A13_A14_A15.pin4, Mega.A11
  N15: A8_A9_A10_A11_A12_A13_A14_A15.pin5, Mega.A12
  N16: A8_A9_A10_A11_A12_A13_A14_A15.pin6, Mega.A13
  N17: A8_A9_A10_A11_A12_A13_A14_A15.pin7, Mega.A14
  N18: A8_A9_A10_A11_A12_A13_A14_A15.pin8, Mega.A15
  N19: 7seg.pin2, H1.pin1, Mega.D7_PWM
  N20: 7seg.pin3, H1.pin2, Mega.D6_PWM
  N21: 7seg.pin4, H1.pin3, Mega.D5_PWM
  N22: 13_12_11_10_09_08.pin1, Mega.D13_PWM
  N23: 13_12_11_10_09_08.pin2, Mega.D12_PWM
  N24: 13_12_11_10_09_08.pin3, Mega.D11_PWM
  N25: 13_12_11_10_09_08.pin4, Mega.D10_PWM
  N26: 13_12_11_10_09_08.pin5, Mega.D9_PWM
  N27: 13_12_11_10_09_08.pin6, Mega.D8_PWM
  N28: 14_15_16_17_18_19.pin1, Mega.D14/TX3
  N29: 14_15_16_17_18_19.pin2, Mega.D15/RX3
  N30: 14_15_16_17_18_19.pin3, Mega.D16_PWM/TX2
  N31: 14_15_16_17_18_19.pin4, Mega.D17_PWM/RX2
  N32: 14_15_16_17_18_19.pin5, Mega.D18/TX1
  N33: 14_15_16_17_18_19.pin6, Mega.D19/RX1
  N34: I2C.pin1, J8'.pin1, J8''.pin1, J8'''.pin1, J8''''.pin1, J8'''''.pin1, J8''''''.pin1, H2.pin1, Mega.D21/SCL, Mega.SCL
  N35: I2C.pin2, J8'.pin2, J8''.pin2, J8'''.pin2, J8''''.pin2, J8'''''.pin2, J8''''''.pin2, H2.pin2, Mega.D20/SDA, Mega.SDA
  N36: 53_51_49_47_45_43_41_39_37_35_33_31_29_27_25_23.pin1, Mega.D23
  N37: 53_51_49_47_45_43_41_39_37_35_33_31_29_27_25_23.pin2, Mega.D25
  N38: 53_51_49_47_45_43_41_39_37_35_33_31_29_27_25_23.pin3, Mega.D27
  N39: 53_51_49_47_45_43_41_39_37_35_33_31_29_27_25_23.pin4, Mega.D29
  N40: 53_51_49_47_45_43_41_39_37_35_33_31_29_27_25_23.pin5, Mega.D31
  N41: 53_51_49_47_45_43_41_39_37_35_33_31_29_27_25_23.pin6, Mega.D33
  N42: 53_51_49_47_45_43_41_39_37_35_33_31_29_27_25_23.pin7, Mega.D35
  N43: 53_51_49_47_45_43_41_39_37_35_33_31_29_27_25_23.pin8, Mega.D37
  N44: 53_51_49_47_45_43_41_39_37_35_33_31_29_27_25_23.pin9, Mega.D39
  N45: 53_51_49_47_45_43_41_39_37_35_33_31_29_27_25_23.pin10, Mega.D41
  N46: 53_51_49_47_45_43_41_39_37_35_33_31_29_27_25_23.pin11, Mega.D43
  N47: 53_51_49_47_45_43_41_39_37_35_33_31_29_27_25_23.pin12, Mega.D45
  N48: 53_51_49_47_45_43_41_39_37_35_33_31_29_27_25_23.pin13, Mega.D47
  N49: 53_51_49_47_45_43_41_39_37_35_33_31_29_27_25_23.pin14, Mega.D49
  N50: 53_51_49_47_45_43_41_39_37_35_33_31_29_27_25_23.pin15, Mega.D51
  N51: 53_51_49_47_45_43_41_39_37_35_33_31_29_27_25_23.pin16, Mega.D53
  N52: 04_03_02_01_00.pin1, Mega.D4_PWM
  N53: 04_03_02_01_00.pin2, Mega.D3_PWM
  N54: 04_03_02_01_00.pin3, Mega.D2_PWM
  N55: 04_03_02_01_00.pin4, Mega.D1_TX0
  N56: 04_03_02_01_00.pin5, Mega.D0_RX0
  N57: 3_3V.pin1, 3_3V.pin2, 3_3V.pin3, 3_3V.pin4, 3_3V.pin5, 3_3V.pin6, 3_3V.pin7, 3_3V.pin8, 3_3V.pin9, 3_3V.pin10, 3_3V.pin11, 3_3V.pin12, 3_3V.pin13, 3_3V.pin14, 3_3V.pin15, VCC0.pin3, Mega.3V3
  N58: RST.pin1, Mega.RESET
  N59: 52_50_48_46_44_42_40_38_36_34_32_30_28_26_24_22.pin1, Mega.D22
  N60: 52_50_48_46_44_42_40_38_36_34_32_30_28_26_24_22.pin2, Mega.D24
  N61: 52_50_48_46_44_42_40_38_36_34_32_30_28_26_24_22.pin3, Mega.D26
  N62: 52_50_48_46_44_42_40_38_36_34_32_30_28_26_24_22.pin4, Mega.D28
  N63: 52_50_48_46_44_42_40_38_36_34_32_30_28_26_24_22.pin5, Mega.D30
  N64: 52_50_48_46_44_42_40_38_36_34_32_30_28_26_24_22.pin6, Mega.D32
  N65: 52_50_48_46_44_42_40_38_36_34_32_30_28_26_24_22.pin7, Mega.D34
  N66: 52_50_48_46_44_42_40_38_36_34_32_30_28_26_24_22.pin8, Mega.D36
  N67: 52_50_48_46_44_42_40_38_36_34_32_30_28_26_24_22.pin9, Mega.D38
  N68: 52_50_48_46_44_42_40_38_36_34_32_30_28_26_24_22.pin10, Mega.D40
  N69: 52_50_48_46_44_42_40_38_36_34_32_30_28_26_24_22.pin11, Mega.D42
  N70: 52_50_48_46_44_42_40_38_36_34_32_30_28_26_24_22.pin12, Mega.D44
  N71: 52_50_48_46_44_42_40_38_36_34_32_30_28_26_24_22.pin13, Mega.D46
  N72: 52_50_48_46_44_42_40_38_36_34_32_30_28_26_24_22.pin14, Mega.D48
  N73: 52_50_48_46_44_42_40_38_36_34_32_30_28_26_24_22.pin15, Mega.D50
  N74: 52_50_48_46_44_42_40_38_36_34_32_30_28_26_24_22.pin16, Mega.D52
